// Logisim project Calculadora_Acumuladora_4bit.circ as structural Verilog: 7 circuits, main circuit Calculadora_Top
module Sumador_1bit (
  input  A,
  input  B,
  input  Cin,
  output S,
  output Cout
);

  wire and_1_out, and_2_out, or_1_p3, xor_1_p1;

  // XOR_Gate xor_1: pin names not known; wires that end beside it: xor_1_p1, B, Cin, A
  // XOR_Gate xor_2 has open pins: in0=xor_1_p1, out=open
  // AND_Gate and_1 has open pins: out=and_1_out
  // AND_Gate and_2 has open pins: out=and_2_out
  // OR_Gate or_1: pin names not known; wires that end beside it: and_1_out, and_2_out, or_1_p3, or_1_p3
endmodule

module Sumador_4bit_RCA (
  input  [3:0] A,
  input  [3:0] B,
  input  Cin,
  output [3:0] S,
  output Cout
);

  // Adder #(.width(4)) adder_1: pin names not known; wires that end beside it: A, B, B, Cin, S, Cout
endmodule

module SumRes_4bit (
  input  [3:0] A,
  input  [3:0] B,
  input  Op,
  output [3:0] Result,
  output Cout
);

  // XOR_Gate #(.width(4)) xor_1: pin names not known; wires that end beside it: Op, B
  // Adder #(.width(4)) adder_1: pin names not known; wires that end beside it: Op, A, Result, Cout
endmodule

module Registro_4bit_EN (
  input  [3:0] D,
  input  CLK,
  input  EN,
  input  RST,
  output [3:0] Q
);

  Register #(.width(4), .trigger("rising")) REG (.clk(RST), .clr(CLK));  // open: D, en, Q
endmodule

module FSM_Control (
  input  START,
  input  CLK,
  input  RST,
  output LD_A,
  output LD_B,
  output LD_ACC,
  output EN_DISP,
  output [1:0] STATE_OUT
);

  Register #(.width(2), .trigger("rising")) STATE ();  // open: D, en, Q, clk, clr
  Decoder #(.select(2), .enable("false")) decoder_1 ();  // open: out0, out1, out2, out3, sel
endmodule

module BCD_7seg (
  input  [3:0] BCD
);

  Hex_Digit_Display hex_digit_display_1 (.value(BCD));  // open: dp
endmodule

module Calculadora_Top (
  input  [3:0] SW_A,
  input  [3:0] SW_B,
  input  OP,
  input  START,
  input  CLK,
  input  RST
);

  wire adder_1_p4, REG_A_p3, REG_B_p2, text_4_p1;

  // Text text_1: pin names not known; wires that end beside it: START
  // Text text_2: pin names not known; wires that end beside it: RST
  // Register #(.width(4), .trigger("rising")) REG_A: pin names not known; wires that end beside it: SW_A, CLK, REG_A_p3
  // Register #(.width(4), .trigger("rising")) REG_B: pin names not known; wires that end beside it: SW_B, REG_B_p2
  // XOR_Gate #(.width(4)) xor_1: pin names not known; wires that end beside it: REG_B_p2, OP, OP
  // Text text_3: pin names not known
  // Adder #(.width(4)) adder_1: pin names not known; wires that end beside it: OP, REG_A_p3, OP, adder_1_p4
  // Register #(.width(4), .trigger("rising")) ACC: pin names not known; wires that end beside it: adder_1_p4
  // Text text_4: pin names not known; wires that end beside it: text_4_p1, text_4_p1
  Hex_Digit_Display DISPLAY ();  // open: value, dp
  LED DAC_b3 ();  // open: in
  LED OVF ();  // open: in
  LED DAC_b2 ();  // open: in
  LED DAC_b1 ();  // open: in
  LED DAC_b0 ();  // open: in
endmodule
